# Fritzing sketch Arduino_Uno_and_HC05_Module (saved by Fritzing 0.9.3b)

parts:
  Part1 = Arduino Uno (Rev3)
  Part2 = Bluetooth HC-05 Macho

nets:
  N1: Part1.D9_PWM, Part2.Key
  N2: Part1.D10_PWM/SS, Part2.TXD
  N3: Part1.D11_PWM/MOSI, Part2.RXD
  5V: Part1.5V, Part2.VCC
  GND: Part1.GND, Part2.GND
